# Fritzing sketch Plan (saved by Fritzing 1.0.4)
breadboards: 2

parts:
  Bat2 = battery_holder_single_18650
  A1 = BMS 1S 5A
  M1 = TP4056 Module [part_number=HW-107]
  A2 = CN3065 Mini Solar Charger Module
  J1 = Wago 221-415
  J2 = Wago 221-415
  D2 = Schottky Diode [part_number=1N5817 package="300 mil [THT]"]
  D1 = Schottky Diode [part_number=1N5817 package="300 mil [THT]"]
  M2 = INA219 DC Current Monitor Module [part_number=CJMCU]
  M3 = DOIT Esp32 DevKit v1 (30 pins long, 11 pins width) [part_number=ESP32S-PIN30]
  LCD1 = 2.8" SPI TFT Module [part_number=MSP2807]
  M4 = BME280 [part_number=GYBMEP]
  Part1 = Adafruit ADS1115 16Bit I2C ADC [part_number="Adafruit #1085"]
  U1 = WS2812 RGB LED matrix 1x8

nets:
  N1: Bat2.+#0, A1.Pin_3
  N2: Bat2.+#1, M2.Vin+
  N3: A1.Pin_1, M2.Vin-
  VIN: A1.Pin_2, J2.Pin_2, J2.Pin_3, J2.Pin_4, J2.Pin_5, D2.cathode, D1.cathode, M3.VIN, U1.VCC
  GND: A1.Pin_4, M1.BAT-, A2.Pin_4, A2.Pin_10, A2.Pin_12, J1.Pin_2, J1.Pin_3, J1.Pin_4, J1.Pin_5, M2.GND, M3.GND, LCD1.pin2, M4.GND, Part1.GND, U1.GND
  N4: M1.BAT+, D1.anode
  N5: A2.Pin_11, D2.anode
  VCC: M2.VCC, M3.3V3, LCD1.pin1, M4.VIN, Part1.VDD

custom parts:
  battery_holder_single_18650: single 18650 battery holder
  BMS 1S 5A: 1S 5A 3.7V li-ion 3BMS PCM battery protection board.
  TP4056 Module: TP4056 Lithium Battery Charge Management Module Links: TP4056 website
  CN3065 Mini Solar Charger Module: CN3791 MPPT Solar Panel Regulator Controller 6V 9V 12V 1 Zelle Lithium-Batterie Ladung Solar Panel Ladegerät board-Controller Module.
  Wago 221-415: Wago 221-415 5 position splicing connector 12AWG.
  INA219 DC Current Monitor Module: INA219 DC Current Monitor Module Links: INA219 product information
  DOIT Esp32 DevKit v1 (30 pins long, 11 pins width): The DOIT Esp32 DevKit v1 is one of the development board created by DOIT to evaluate the ESP-WROOM-32 module. It is based on the ESP32 microcontroller that boasts Wifi, Bluetooth, Ethernet and Low Power support all in a single chip. (vanepp) made breadboard work, adjusted pin numbering and labels and reduced size of schematic and cleaned up pcb. This chip is 30pins long (2 x15) and 11 pins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
  2.8" SPI TFT Module: A generic 2.8 inch LCD TFT 320x240 display with touchscreen and SD card slot. Uses the ILI9341 controller, like the Adafruit displays of this size uses.
  BME280: Generic Bosch Sensortec BME280, temperature, humidity and barometric pressure sensor module (I2C interface)
  Adafruit ADS1115 16Bit I2C ADC: For microcontrollers without an analog-to-digital converter or when you want a higher-precision ADC, the ADS1115 provides 16-bit precision at 860 samples/second over I2C. The chip can be configured as 4 single-ended input channels, or two differential channels. As a nice bonus, it even includes a programmable gain amplifier, up to x16, to help boost up smaller single/differential signals to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
  WS2812 RGB LED matrix 1x8: WS2812 matrix 1x8
